# Fritzing sketch bikonect-IoT (saved by Fritzing 0.9.3b)
breadboards: 1

parts:
  Componente1 = Arduino Uno (Rev3)
  Componente2 = Bluetooth HC-05 Macho
  J1 = Basic Servo

nets:
  N1: Componente1.D0/RX, Componente2.TXD
  N2: Componente1.D1/TX, Componente2.RXD
  N3: Componente1.D6_PWM, J1.pulse
  VCC: Componente1.5V, Componente2.VCC, J1.vcc
  GND: Componente1.GND, Componente2.GND, J1.gnd
